// Logisim project bfcpu.circ as structural Verilog: 7 circuits, main circuit Register4
module main (
  input  RESET,
  input  EN_D,
  input  EN_DP,
  input  EN_SP,
  input  EN_F,
  input  EN_I,
  input  EN_IP,
  input  EN_LS,
  input  LD_D,
  input  LD_DP,
  input  LD_SP,
  input  LD_F,
  input  LD_I,
  input  LD_IP,
  input  LD_LS,
  input  [2:0] RS,
  input  INC,
  input  DEC,
  input  WE,
  input  OE,
  input  PRE,
  input  [3:0] in_22,
  input  [3:0] in_23
);

  wire AE, CLC, LD_I_t, RESET_t, VE, Z_D, Z_LS;
  wire [1:0] DPREG, DREG, FREG, IPREG, IREG, LSREG, SPREG, undriven;
  wire [3:0] F_d_out, programrom_1_cmd;
  wire [7:0] DOUT, IP_d_out;
  wire [15:0] DP_d_out, RAM1_dout;

  RAM #(.addrWidth(16), .clearpin("true")) RAM1 (
    .addr(DP_d_out), .we(WE), .oe(OE), .clk(CLC), .din(DOUT), .dout(RAM1_dout[7:0]), .clr(RESET));
  RegisterDriver registerdriver_1 (
    .INC(INC), .DEC(DEC), .CLC(CLC), .RS(RS), .R0(DREG), .R1(DPREG), .R2(SPREG), .R3(FREG), .R4(IREG),
    .R5(IPREG), .R6(LSREG));  // open: R7
  Register16 DP (
    .D_IN(16'h100), .CLC(CLC), .EN(EN_DP), .LD(RESET), .DN(DPREG[0]), .UP(DPREG[1]), .D_OUT(DP_d_out));  // open: RESET, Z
  // Register8 D: pin names not known; wires that end beside it: CLC, EN_D, LD_D, DREG[0], DREG[1], RESET, RAM1_dout[7:0], Z_D, DOUT
  RAM #(.addrWidth(16), .clearpin("true")) RAM2 (
    .addr(DP_d_out), .we(WE), .oe(OE), .clk(CLC), .din(IP_d_out), .dout(RAM1_dout[15:8]), .clr(RESET));
  Register16 SP (
    .RESET(RESET), .CLC(CLC), .EN(EN_SP), .LD(LD_SP), .DN(SPREG[0]), .UP(SPREG[1]), .D_OUT(DP_d_out));  // open: D_IN, Z
  Register4 F (
    .EN(EN_F), .LD(LD_F), .CLC(CLC), .D_IN({undriven, VE, AE}), .RESET(RESET_t), .D_OUT(F_d_out));  // open: DN, UP, Z
  Register16 IP (
    .D_IN(RAM1_dout), .RESET(RESET), .CLC(CLC), .EN(EN_IP), .LD(LD_IP), .DN(IPREG[0]), .UP(IPREG[1]),
    .D_OUT({IP_d_out, DOUT}));  // open: Z
  ProgramROM programrom_1 (.ADDR({IP_d_out, DOUT}), .CMD(programrom_1_cmd));
  // Register8 LS: pin names not known; wires that end beside it: CLC, EN_LS, LD_LS, LSREG[0], LSREG[1], RESET_t, Z_LS
  TTY tty_1 (.data(DOUT[6:0]), .clk(CLC), .we(PRE), .clr(RESET_t));
  Register8 I (
    .LD(LD_I_t), .D_IN({Z_D, Z_LS, F_d_out[1:0], programrom_1_cmd}));  // open: RESET, CLC, EN, DN, UP, Z, D_OUT
  Clock clock_1 (.out(CLC));
  ControlUnit controlunit_1 (
    .CLC(CLC), .CMD(in_22), .FLAGS(in_23), .LD_I(LD_I_t));  // open: RS, INC, DEC, EN_D, EN_DP, EN_IP, EN_SP, OE_RAM, WE_RAM, LD_D, LD_IP, LD_F, CR, VE, AE, PRE, ERR

  // Other names for the same wires on the sheet: R = RESET

  // Notes on the sheet:
  //   RESET VECTOR
endmodule

module Register4 (
  input  CLC,
  input  EN,
  input  LD,
  input  DN,
  input  UP,
  input  [3:0] D_IN,
  input  RESET,
  output [3:0] D_OUT,
  output Z
);

  wire n74193_1_pin11;
  wire [3:0] n74193_1_pin3;

  _74193 u_74193_1 (
    .pin1(D_IN[1]), .pin2(n74193_1_pin3[1]), .pin3(n74193_1_pin3[0]), .pin4(DN), .pin5(UP),
    .pin6(n74193_1_pin3[2]), .pin7(n74193_1_pin3[3]), .pin15(D_IN[0]), .pin14(RESET), .pin11(n74193_1_pin11),
    .pin10(D_IN[2]), .pin9(D_IN[3]));  // open: pin13, pin12
  nand nand_1 (n74193_1_pin11, LD, CLC);
  Hex_Digit_Display hex_digit_display_1 (.value(n74193_1_pin3));  // open: dp
  nor nor_1 (Z, n74193_1_pin3[3], n74193_1_pin3[2], n74193_1_pin3[1], n74193_1_pin3[0]);
  assign D_OUT = EN ? n74193_1_pin3 : 4'bz;  // Controlled_Buffer controlled_buffer_1
endmodule

module Register8 (
  input  [7:0] D_IN,
  input  CLC,
  input  EN,
  input  LD,
  input  DN,
  input  UP,
  input  RESET,
  output [7:0] D_OUT,
  output Z
);

  wire n74193_1_pin12, n74193_1_pin13, nand_1_out, or_1_out, or_2_out;
  wire [3:0] n74193_1_pin3, n74193_2_pin3;

  nand nand_1 (nand_1_out, CLC, LD);
  _74193 u_74193_1 (
    .pin1(D_IN[1]), .pin2(n74193_1_pin3[1]), .pin3(n74193_1_pin3[0]), .pin4(DN), .pin5(UP),
    .pin6(n74193_1_pin3[2]), .pin7(n74193_1_pin3[3]), .pin15(D_IN[0]), .pin14(RESET), .pin13(n74193_1_pin13),
    .pin12(n74193_1_pin12), .pin11(nand_1_out), .pin10(D_IN[2]), .pin9(D_IN[3]));
  Hex_Digit_Display hex_digit_display_1 (.value(n74193_1_pin3));  // open: dp
  or or_1 (or_1_out, n74193_1_pin3[3], n74193_1_pin3[2], n74193_1_pin3[1], n74193_1_pin3[0]);
  assign D_OUT[7:4] = EN ? n74193_1_pin3 : 4'bz;  // Controlled_Buffer controlled_buffer_1
  _74193 u_74193_2 (
    .pin1(D_IN[5]), .pin2(n74193_2_pin3[1]), .pin3(n74193_2_pin3[0]), .pin4(n74193_1_pin13),
    .pin5(n74193_1_pin12), .pin6(n74193_2_pin3[2]), .pin7(n74193_2_pin3[3]), .pin15(D_IN[4]), .pin14(RESET),
    .pin11(nand_1_out), .pin10(D_IN[6]), .pin9(D_IN[7]));  // open: pin13, pin12
  Hex_Digit_Display hex_digit_display_2 (.value(n74193_2_pin3));  // open: dp
  or or_2 (or_2_out, n74193_2_pin3[3], n74193_2_pin3[2], n74193_2_pin3[1], n74193_2_pin3[0]);
  assign D_OUT[3:0] = EN ? n74193_2_pin3 : 4'bz;  // Controlled_Buffer controlled_buffer_2
  nor nor_1 (Z, or_2_out, or_1_out);

  // Other names for the same wires on the sheet: R = RESET
endmodule

module Register16 (
  input  [15:0] D_IN,
  input  CLC,
  input  EN,
  input  LD,
  input  DN,
  input  UP,
  input  RESET,
  output [15:0] D_OUT,
  output Z
);

  wire n74193_1_pin12, n74193_1_pin13, n74193_2_pin12, n74193_2_pin13, n74193_3_pin12, n74193_3_pin13,
       nand_1_out, or_1_out, or_2_out, or_3_out, or_4_out;
  wire [3:0] n74193_1_pin3, n74193_2_pin3, n74193_3_pin3, n74193_4_pin3;

  nand nand_1 (nand_1_out, CLC, LD);
  _74193 u_74193_1 (
    .pin1(D_IN[1]), .pin2(n74193_1_pin3[1]), .pin3(n74193_1_pin3[0]), .pin4(DN), .pin5(UP),
    .pin6(n74193_1_pin3[2]), .pin7(n74193_1_pin3[3]), .pin15(D_IN[0]), .pin14(RESET), .pin13(n74193_1_pin13),
    .pin12(n74193_1_pin12), .pin11(nand_1_out), .pin10(D_IN[2]), .pin9(D_IN[3]));
  or or_1 (or_1_out, n74193_1_pin3[3], n74193_1_pin3[2], n74193_1_pin3[1], n74193_1_pin3[0]);
  Hex_Digit_Display hex_digit_display_1 (.value(n74193_1_pin3));  // open: dp
  assign D_OUT[3:0] = EN ? n74193_1_pin3 : 4'bz;  // Controlled_Buffer controlled_buffer_1
  _74193 u_74193_2 (
    .pin1(D_IN[5]), .pin2(n74193_2_pin3[1]), .pin3(n74193_2_pin3[0]), .pin4(n74193_1_pin13),
    .pin5(n74193_1_pin12), .pin6(n74193_2_pin3[2]), .pin7(n74193_2_pin3[3]), .pin15(D_IN[4]), .pin14(RESET),
    .pin13(n74193_2_pin13), .pin12(n74193_2_pin12), .pin11(nand_1_out), .pin10(D_IN[6]), .pin9(D_IN[7]));
  Hex_Digit_Display hex_digit_display_2 (.value(n74193_2_pin3));  // open: dp
  or or_2 (or_2_out, n74193_2_pin3[3], n74193_2_pin3[2], n74193_2_pin3[1], n74193_2_pin3[0]);
  assign D_OUT[7:4] = EN ? n74193_2_pin3 : 4'bz;  // Controlled_Buffer controlled_buffer_2
  _74193 u_74193_3 (
    .pin1(D_IN[9]), .pin2(n74193_3_pin3[1]), .pin3(n74193_3_pin3[0]), .pin4(n74193_2_pin13),
    .pin5(n74193_2_pin12), .pin6(n74193_3_pin3[2]), .pin7(n74193_3_pin3[3]), .pin15(D_IN[8]), .pin14(RESET),
    .pin13(n74193_3_pin13), .pin12(n74193_3_pin12), .pin11(nand_1_out), .pin10(D_IN[10]), .pin9(D_IN[11]));
  Hex_Digit_Display hex_digit_display_3 (.value(n74193_3_pin3));  // open: dp
  or or_3 (or_3_out, n74193_3_pin3[3], n74193_3_pin3[2], n74193_3_pin3[1], n74193_3_pin3[0]);
  assign D_OUT[11:8] = EN ? n74193_3_pin3 : 4'bz;  // Controlled_Buffer controlled_buffer_3
  _74193 u_74193_4 (
    .pin1(D_IN[13]), .pin2(n74193_4_pin3[1]), .pin3(n74193_4_pin3[0]), .pin4(n74193_3_pin13),
    .pin5(n74193_3_pin12), .pin6(n74193_4_pin3[2]), .pin7(n74193_4_pin3[3]), .pin15(D_IN[12]), .pin14(RESET),
    .pin11(nand_1_out), .pin10(D_IN[14]), .pin9(D_IN[15]));  // open: pin13, pin12
  Hex_Digit_Display hex_digit_display_4 (.value(n74193_4_pin3));  // open: dp
  or or_4 (or_4_out, n74193_4_pin3[3], n74193_4_pin3[2], n74193_4_pin3[1], n74193_4_pin3[0]);
  assign D_OUT[15:12] = EN ? n74193_4_pin3 : 4'bz;  // Controlled_Buffer controlled_buffer_4
  nor nor_1 (Z, or_4_out, or_3_out, or_2_out, or_1_out);

  // Other names for the same wires on the sheet: R = RESET
endmodule

module RegisterDriver (
  input  INC,
  input  DEC,
  input  CLC,
  input  [2:0] RS,
  output [1:0] R0,
  output [1:0] R1,
  output [1:0] R2,
  output [1:0] R3,
  output [1:0] R4,
  output [1:0] R5,
  output [1:0] R6,
  output [1:0] R7
);

  wire and_1_out, not_1_out, not_2_out, xor_1_out;
  wire [1:0] nand_1_out;

  xor xor_1 (xor_1_out, DEC, INC);
  not not_1 (not_1_out, INC);
  not not_2 (not_2_out, DEC);
  and and_1 (and_1_out, xor_1_out, CLC);
  nand nand_1 (nand_1_out[0], not_1_out, and_1_out);
  nand nand_2 (nand_1_out[1], not_2_out, and_1_out);
  Demultiplexer #(.select(3), .width(2)) demultiplexer_1 (
    .out0(R0), .out1(R1), .out2(R2), .out3(R3), .out4(R4), .out5(R5), .out6(R6), .out7(R7), .in(nand_1_out),
    .sel(RS));
endmodule

module ControlUnit (
  input  [3:0] CMD,
  input  [3:0] FLAGS,
  input  CLC,
  output [2:0] RS,
  output INC,
  output DEC,
  output EN_D,
  output EN_DP,
  output EN_IP,
  output EN_SP,
  output OE_RAM,
  output WE_RAM,
  output LD_D,
  output LD_IP,
  output LD_I,
  output LD_F,
  output CR,
  output VE,
  output AE,
  output PRE,
  output ERR
);

  wire n74163_1_pin1, n74163_1_pin7, not_2_out;
  wire [2:0] n74163_1_pin14;
  wire [3:3] n74163_1_pin11;
  wire [7:4] ROM3_data;
  wire [24:0] multiplexer_1_out;

  Multiplexer #(.select(4), .width(25)) multiplexer_1 (
    .in0(25'h1f4105f), .in1(25'h427c84), .in2(25'h421084), .in3(25'h454400), .in4(25'h4544), .in5(25'h35c0),
    .in6(25'h10035c0), .in7(25'h18c0), .in8(25'hfc400), .in9(25'h47e0), .out(multiplexer_1_out), .sel(CMD));  // open: in10, in11, in12, in13, in14, in15
  ROM #(.addrWidth(13)) ROM1 (.addr({2'b00, CMD, n74163_1_pin14, FLAGS}), .data({EN_IP, EN_DP, EN_D, DEC, INC, RS}));
  Hex_Digit_Display hex_digit_display_1 (.value(CMD));  // open: dp
  DotMatrix #(.matrixrows(5)) dotmatrix_1 (
    .col0(multiplexer_1_out[24:20]), .col1(multiplexer_1_out[19:15]), .col2(multiplexer_1_out[14:10]),
    .col3(multiplexer_1_out[9:5]), .col4(multiplexer_1_out[4:0]));
  ROM #(.addrWidth(13)) ROM2 (
    .addr({2'b00, CMD, n74163_1_pin14, FLAGS}), .data({CR, LD_F, LD_I, LD_IP, LD_D, WE_RAM, OE_RAM, EN_SP}));
  _74163 u_74163_1 (
    .pin1(n74163_1_pin1), .pin2(CLC), .pin7(n74163_1_pin7), .pin14(n74163_1_pin14[0]),
    .pin13(n74163_1_pin14[1]), .pin12(n74163_1_pin14[2]), .pin11(n74163_1_pin11[3]), .pin10(n74163_1_pin7));  // open: pin3, pin4, pin5, pin6, pin15, pin9
  not not_1 (n74163_1_pin1, CR);
  not not_2 (not_2_out, ERR);
  LED led_1 (.in(not_2_out));
  LED led_2 (.in(ERR));
  Hex_Digit_Display hex_digit_display_2 (.value({n74163_1_pin11[3], n74163_1_pin14}));  // open: dp
  ROM #(.addrWidth(13)) ROM3 (.addr({2'b00, CMD, n74163_1_pin14, FLAGS}), .data({ROM3_data, ERR, PRE, AE, VE}));
  // also tied to VCC on the sheet: n74163_1_pin7

  // Notes on the sheet:
  //   contents of ROM1 (hex, n*v repeats v):
  //   16*80 112*0 16*80 d d 8 8 d d 40 40 d d 8 8 d d 40 40 0 0 d d 6*0 d d 84*0 16*80 d d 10 10 d d 40 40
  //   d d 10 10 d d 40 40 0 0 d d 6*0 d d 84*0 16*80 d d 11 11 d d 11 11 d d 60 60 d d 60 60 0 0 d d 0 0 d
  //   d 88*0 16*80 d d 9 9 d d 9 9 d d 60 60 d d 60 60 0 0 d d 0 0 d d 88*0 16*80 112*0 16*80 112*0 16*80
  //   d d 2d 2d d d 40 40 d d 2d 2d d d 40 40 6*0 2d 2d 6*0 2d 2d 80*0 16*80 e e a e e e 40 40 e e a e e e
  //   40 40 d d 80 b d d 0 0 d d 80 b d d 4*0 d 7*0 d 69*0 16*80 16 16 0 12 16 16 40 40 16 16 0 12 16 16
  //   40 40 6*d 0 0 6*d 82*0 16*80 112*0 16*80 112*0 16*80 112*0 16*80 112*0 16*80 112*0 16*80
  //   Cycle Count
  //   contents of ROM2 (hex, n*v repeats v):
  //   16*20 112*80 16*20 80 80 40 40 80 80 ca ca 80 80 40 40 80 80 ca ca 96*80 16*20 80 80 40 40 80 80 ca
  //   ca 80 80 40 40 80 80 ca ca 96*80 16*20 80 80 40 40 80 80 40 40 80 80 c4 c4 80 80 c4 c4 96*80 16*20
  //   80 80 40 40 80 80 40 40 80 80 c4 c4 80 80 c4 c4 96*80 16*20 112*80 16*20 112*80 16*20 6*80 a a 6*80
  //   a a 96*80 16*20 6*0 a a 6*0 a a 80 80 5 80 80 80 c0 c0 80 80 5 80 80 80 c0 c0 80*80 16*20 0 0 13 0 0
  //   0 a a 0 0 13 0 0 0 a a 6*80 c0 c0 6*80 c0 c0 80*80 16*20 112*80 16*20 112*80 16*20 112*80 16*20
  //   112*80 16*20 112*80 16*20 112*80
  //   contents of ROM3 (hex, n*v repeats v):
  //   16*0 112*8 18*0 1 1 6*0 1 1 4*0 8 8 0 0 6*8 0 0 84*8 18*0 1 1 6*0 1 1 4*0 8 8 0 0 6*8 0 0 84*8 18*0
  //   2 2 0 0 2 2 8*0 8 8 0 0 8 8 0 0 88*8 18*0 2 2 0 0 2 2 8*0 8 8 0 0 8 8 0 0 88*8 16*0 112*8 16*0 112*8
  //   18*0 4 4 6*0 4 4 4*0 6*8 4 4 6*8 4 4 80*8 48*0 8 8 0 7*8 0 69*8 48*0 80*8 16*0 112*8 16*0 112*8 16*0
  //   112*8 16*0 112*8 16*0 112*8 16*0 112*8
endmodule

module ProgramROM (
  input  [15:0] ADDR,
  output [3:0] CMD
);

  wire [7:0] rom_1_data;

  ROM #(.addrWidth(13)) rom_1 (.addr(ADDR[13:1]), .data(rom_1_data));
  Multiplexer multiplexer_1 (.in0(rom_1_data[0]), .in1(rom_1_data[4]), .out(CMD[0]), .sel(ADDR[0]));
  Multiplexer multiplexer_2 (.in0(rom_1_data[1]), .in1(rom_1_data[5]), .out(CMD[1]), .sel(ADDR[0]));
  Multiplexer multiplexer_3 (.in0(rom_1_data[2]), .in1(rom_1_data[6]), .out(CMD[2]), .sel(ADDR[0]));
  Multiplexer multiplexer_4 (.in0(rom_1_data[3]), .in1(rom_1_data[7]), .out(CMD[3]), .sel(ADDR[0]));

  // Notes on the sheet:
  //   contents of rom_1 (hex, n*v repeats v):
  //   12 34 56 78
endmodule
